# Fritzing sketch ESP8266-12_mini_breakout_v0.2 (saved by Fritzing 0.9.3b)
circuit board: 2.9cm x 3.1cm
breadboards: 1

parts:
  ESP8267 = ESP8266 WiFi Module [part_number=ESP8266]
  Pad1 = Pad [width=1.2 height=3 connect=center]  # not connected
  Pad2 = Pad [width=1.2 height=3 connect=center]  # not connected
  Pad3 = Pad [width=1.2 height=3 connect=center]  # not connected
  Pad4 = Pad [width=1.2 height=3 connect=center]  # not connected
  Pad5 = Pad [width=1.2 height=3 connect=center]  # not connected
  Pad6 = Pad [width=1.2 height=3 connect=center]  # not connected
  Pad7 = Pad [width=1.2 height=3 connect=center]  # not connected
  Pad8 = Pad [width=1.2 height=3 connect=center]  # not connected
  Pad9 = Pad [width=1.2 height=3 connect=center]  # not connected
  Pad10 = Pad [width=1.2 height=3 connect=center]  # not connected
  Pad11 = Pad [width=1.2 height=3 connect=center]  # not connected
  Pad12 = Pad [width=1.2 height=3 connect=center]  # not connected
  Pad13 = Pad [width=1.2 height=3 connect=center]  # not connected
  Pad14 = Pad [width=1.2 height=3 connect=center]  # not connected
  Pad15 = Pad [width=1.2 height=3 connect=center]  # not connected
  Pad16 = Pad [width=1.2 height=3 connect=center]  # not connected
  R1 = Resistor [tolerance=±5% resistance=4.7k package=THT]
  CON1 = male pin header, 8 pins [form="♂ (male)"]
  CON2 = male pin header, 8 pins [form="♂ (male)"]
  R2 = Resistor [tolerance=±5% resistance=4.7k package=THT]
  R3 = Resistor [tolerance=±5% resistance=4.7k package=THT]
  R4 = Resistor [tolerance=±5% resistance=4.7k package=THT]
  R5 = Resistor [tolerance=±5% resistance=4.7k package=THT]

nets:
  N1: ESP8267.RXD, CON2.pin2
  N2: ESP8267.VCC, R1.Pin_1, CON1.pin8, R2.Pin_1, R3.Pin_1, R4.Pin_1
  N3: ESP8267.GPIO_0, CON2.pin5, R3.Pin_0
  N4: ESP8267.GPIO_2, CON2.pin6, R4.Pin_0
  N5: ESP8267.CH_PD, CON1.pin3, R2.Pin_0
  N6: ESP8267.GND, CON2.pin8, R5.Pin_0
  N7: ESP8267.TXD, CON2.pin1
  N8: ESP8267.GPIO_15, CON2.pin7, R5.Pin_1
  N9: ESP8267.GPIO_4, CON2.pin3
  N10: ESP8267.GPIO_5, CON2.pin4
  N11: ESP8267.ADC_0, CON1.pin2
  N12: ESP8267.GPIO_16, ESP8267.REST, R1.Pin_0, CON1.pin1, CON1.pin4
  N13: ESP8267.GPIO_14, CON1.pin5
  N14: ESP8267.GPIO_12, CON1.pin6
  N15: ESP8267.GPIO_13, CON1.pin7

custom parts:
  ESP8266 WiFi Module: Generic WiFi Module based on the ESP8266 with onboard PCB antenna and UART communications
