# Fritzing sketch ESP8266-12_mini_breakout_v0.3_narrow (saved by Fritzing 0.9.3b)
circuit board: 2.5cm x 3.55023cm
breadboards: 1

parts:
  CON1 = male pin header, 8 pins [form="♂ (male)"]
  CON2 = male pin header, 8 pins [form="♂ (male)"]
  R1 = Resistor [tolerance=±5% resistance=10k package=THT]
  R2 = Resistor [tolerance=±5% resistance=10k package=THT]
  R3 = Resistor [tolerance=±5% resistance=10k package=THT]
  R4 = Resistor [tolerance=±5% resistance=10k package=THT]
  R5 = Resistor [tolerance=±5% resistance=10k package=THT]
  R7 = Resistor [tolerance=±5% resistance=470 package=THT]
  C1 = Ceramic Capacitor [capacitance=470pF package="200 mil [THT, multilayer]"]
  C3 = Ceramic Capacitor [capacitance=100nF package="200 mil [THT, multilayer]"]
  C2 = Tantalum Capacitor [capacitance=47µF package="100 mil [THT, tantalum]"]
  ESP8267 = ESP8266 WiFi Module [part_number=ESP8266]
  Pad1 = Pad [width=2.2000000000000002 height=1.2 connect=center]  # not connected
  Pad2 = Pad [width=2.2000000000000002 height=1.2 connect=center]  # not connected
  Pad3 = Pad [width=2.2000000000000002 height=1.2 connect=center]  # not connected
  Pad4 = Pad [width=2.2000000000000002 height=1.2 connect=center]  # not connected
  Pad5 = Pad [width=2.2000000000000002 height=1.2 connect=center]  # not connected
  Pad6 = Pad [width=2.2000000000000002 height=1.2 connect=center]  # not connected
  Pad7 = Pad [width=2.2000000000000002 height=1.2 connect=center]  # not connected
  Pad8 = Pad [width=2.2000000000000002 height=1.2 connect=center]  # not connected
  Pad9 = Pad [width=2.2000000000000002 height=1.2 connect=center]  # not connected
  Pad10 = Pad [width=2.2000000000000002 height=1.2 connect=center]  # not connected
  Pad11 = Pad [width=2.2000000000000002 height=1.2 connect=center]  # not connected
  Pad12 = Pad [width=2.2000000000000002 height=1.2 connect=center]  # not connected
  Pad13 = Pad [width=2.2000000000000002 height=1.2 connect=center]  # not connected
  Pad14 = Pad [width=2.2000000000000002 height=1.2 connect=center]  # not connected
  Pad15 = Pad [width=2.2000000000000002 height=1.2 connect=center]  # not connected
  Pad16 = Pad [width=2.2000000000000002 height=1.2 connect=center]  # not connected

nets:
  N1: CON1.pin1, R4.Pin_1, R7.Pin_0, C1.1, ESP8267.REST
  N2: CON1.pin2, ESP8267.ADC_0
  N3: CON1.pin5, ESP8267.GPIO_14
  N4: CON1.pin6, ESP8267.GPIO_12
  N5: CON1.pin7, ESP8267.GPIO_13
  N6: CON1.pin8, R1.Pin_0, R2.Pin_0, R3.Pin_0, R4.Pin_0, C3.1, C2.+, ESP8267.VCC
  N7: CON2.pin1, ESP8267.TXD
  N8: CON2.pin2, ESP8267.RXD
  N9: CON2.pin3, ESP8267.GPIO_4
  N10: CON2.pin4, ESP8267.GPIO_5
  N11: CON2.pin5, R2.Pin_1, ESP8267.GPIO_0
  N12: CON2.pin8, R5.Pin_1, C2.-, ESP8267.GND
  N13: R1.Pin_1, ESP8267.CH_PD
  N14: R3.Pin_1, ESP8267.GPIO_2
  N15: R5.Pin_0, ESP8267.GPIO_15
  N16: R7.Pin_1, ESP8267.GPIO_16
  N17: C1.0, C3.0

custom parts:
  ESP8266 WiFi Module: Generic WiFi Module based on the ESP8266 with onboard PCB antenna and UART communications
